// Logisim project 15.circ as structural Verilog: 1 circuit, main circuit main
module main (
  input  in_1,
  input  in_2,
  input  in_3,
  input  in_4,
  output out_5,
  output out_6,
  output out_7,
  output out_8,
  output out_9,
  output out_10
);

  wire clock_1_out, clock_2_out, clock_3_out;

  Clock clock_1 (.out(clock_1_out));
  Clock clock_2 (.out(clock_2_out));
  Clock clock_3 (.out(clock_3_out));
  J_K_Flip_Flop j_k_ff_1 (.J(in_1), .clk(clock_1_out), .K(in_2), .Q(out_5), .Qn(out_6));  // open: preset, en, reset
  J_K_Flip_Flop j_k_ff_2 (.J(clock_2_out), .K(in_3), .Q(out_7), .Qn(out_8));  // open: clk, preset, en, reset
  J_K_Flip_Flop j_k_ff_3 (.J(clock_3_out), .K(in_4), .Q(out_9), .Qn(out_10));  // open: clk, preset, en, reset
endmodule
