// Logisim project DL1.circ as structural Verilog: 1 circuit, main circuit main
module main (
  input  A,
  input  B,
  output y1,
  output y2,
  output y3,
  output y4,
  output y5
);

  and and_1 (y1, A, B);
  or or_1 (y2, A, B);
  not not_1 (y3, A);
  xor xor_1 (y4, A, B);
  xnor xnor_1 (y5, A, B);

  // Notes on the sheet:
  //   z
endmodule
