// Logisim project dl.3 lab.circ as structural Verilog: 1 circuit, main circuit main
module main (
  input  in_1,
  input  in_2,
  input  in_3,
  input  in_4,
  input  in_5,
  input  in_6,
  input  in_7,
  input  in_8,
  output out_9,
  output out_10,
  output out_11,
  output out_12
);

  wire and_1_out, not_3_out, not_4_out, not_5_out, not_6_out, or_1_out;

  or or_1 (or_1_out, in_2, in_3);
  and and_1 (and_1_out, in_5, in_7);
  not not_1 (out_10, or_1_out);
  not not_2 (out_11, and_1_out);
  not not_3 (not_3_out, in_1);
  not not_4 (not_4_out, in_4);
  not not_5 (not_5_out, in_6);
  not not_6 (not_6_out, in_8);
  and and_2 (out_9, not_3_out, not_4_out);
  or or_2 (out_12, not_5_out, not_6_out);

  // Notes on the sheet:
  //   not_2 drives only 1 and floats otherwise
  //   not_3 drives only 1 and floats otherwise
  //   not_4 drives only 1 and floats otherwise
endmodule
