// Logisim project dl.lab 3.c.circ as structural Verilog: 1 circuit, main circuit main
module main (
  input  A,
  input  in_2,
  input  in_3,
  input  in_4,
  input  in_5,
  output y1,
  output out_7,
  output out_8
);

  wire nor_2_out, nor_4_out, nor_5_out;

  nor nor_1 (y1, A, A);
  nor nor_2 (nor_2_out, in_4, in_5);
  not nor_3 (out_8, nor_2_out);  // NOR_Gate
  nor nor_4 (nor_4_out, in_2, in_2);
  nor nor_5 (nor_5_out, in_3, in_3);
  nor nor_6 (out_7, nor_4_out, nor_5_out);
endmodule
